# Fritzing sketch 16-led-segment-layout (saved by Fritzing 0.9.1b)
circuit board: 10.9529cm x 18.0716cm

parts:
  HEAT-7 = LED - 5mm [color="Red (633nm)" package="5 mm [THT]"]
  HEAT-6 = LED - 5mm [color="Red (633nm)" package="5 mm [THT]"]
  HEAT-5 = LED - 5mm [color="Yellow (595nm)" package="5 mm [THT]"]
  HEAT-4 = LED - 5mm [color="Yellow (595nm)" package="5 mm [THT]"]
  HEAT-3 = LED - 5mm [color="Green (565nm)" package="5 mm [THT]"]
  HEAT-2 = LED - 5mm [color="Green (565nm)" package="5 mm [THT]"]
  HEAT-1 = LED - 5mm [color="Green (565nm)" package="5 mm [THT]"]
  HEAT-0 = LED - 5mm [color="Green (565nm)" package="5 mm [THT]"]
  MCP23017 = MCP23017 [chip_label=MCP23017 package="DIP (Dual Inline) [THT]"]
  220 = Resistor [tolerance=±5% resistance=220 package=THT]
  220_2 = Resistor [tolerance=±5% resistance=220 package=THT]
  220_3 = Resistor [tolerance=±5% resistance=220 package=THT]
  220_4 = Resistor [tolerance=±5% resistance=220 package=THT]
  220_5 = Resistor [tolerance=±5% resistance=220 package=THT]
  220_6 = Resistor [tolerance=±5% resistance=220 package=THT]
  220_7 = Resistor [tolerance=±5% resistance=220 package=THT]
  220_8 = Resistor [tolerance=±5% resistance=220 package=THT]
  POWER = Slide Potentiometer [maximum_resistance=100kΩ]
  COOL-0 = LED - 5mm [color="Yellow (595nm)" package="5 mm [THT]"]
  COOL-1 = LED - 5mm [color="Yellow (595nm)" package="5 mm [THT]"]
  COOL-2 = LED - 5mm [color="Yellow (595nm)" package="5 mm [THT]"]
  COOL-3 = LED - 5mm [color="Yellow (595nm)" package="5 mm [THT]"]
  COOL-4 = LED - 5mm [color="Yellow (595nm)" package="5 mm [THT]"]
  COOL-5 = LED - 5mm [color="Yellow (595nm)" package="5 mm [THT]"]
  COOL-6 = LED - 5mm [color="Yellow (595nm)" package="5 mm [THT]"]
  COOL-7 = LED - 5mm [color="Yellow (595nm)" package="5 mm [THT]"]
  220_9 = Resistor [tolerance=±5% resistance=220 package=THT]
  220_10 = Resistor [tolerance=±5% resistance=220 package=THT]
  220_11 = Resistor [tolerance=±5% resistance=220 package=THT]
  220_12 = Resistor [tolerance=±5% resistance=220 package=THT]
  220_13 = Resistor [tolerance=±5% resistance=220 package=THT]
  220_14 = Resistor [tolerance=±5% resistance=220 package=THT]
  220_15 = Resistor [tolerance=±5% resistance=220 package=THT]
  220_16 = Resistor [tolerance=±5% resistance=220 package=THT]
  COOLANT = Rotary Encoder [package=THT]
  EXT = screw terminal, 8 pins
  10k = Resistor [tolerance=±5% resistance=10k package=THT]
  10nF = Ceramic Capacitor [capacitance=100nF package="100 mil [THT, multilayer]"]
  10nF_2 = Ceramic Capacitor [capacitance=100nF package="100 mil [THT, multilayer]"]
  10k_2 = Resistor [tolerance=±5% resistance=10k package=THT]
  10k_3 = Resistor [tolerance=±5% resistance=10k package=THT]
  10k_4 = Resistor [tolerance=±5% resistance=10k package=THT]

nets:
  N1: HEAT-7.cathode, 220_8.Pin_0
  N2: HEAT-7.anode, MCP23017.GPA7
  N3: HEAT-6.cathode, 220_7.Pin_0
  N4: HEAT-6.anode, MCP23017.GPA6
  N5: HEAT-5.cathode, 220_6.Pin_0
  N6: HEAT-5.anode, MCP23017.GPA5
  N7: HEAT-4.cathode, 220_5.Pin_0
  N8: HEAT-4.anode, MCP23017.GPA4
  N9: HEAT-3.cathode, 220.Pin_0
  N10: HEAT-3.anode, MCP23017.GPA3
  N11: HEAT-2.cathode, 220_2.Pin_0
  N12: HEAT-2.anode, MCP23017.GPA2
  N13: HEAT-1.cathode, 220_3.Pin_0
  N14: HEAT-1.anode, MCP23017.GPA1
  N15: HEAT-0.cathode, 220_4.Pin_0
  N16: HEAT-0.anode, MCP23017.GPA0
  N17: MCP23017.GPB0, COOL-3.anode
  N18: MCP23017.GPB1, COOL-2.anode
  N19: MCP23017.GPB2, COOL-1.anode
  N20: MCP23017.GPB3, COOL-0.anode
  N21: MCP23017.GPB4, COOL-7.anode
  N22: MCP23017.GPB5, COOL-6.anode
  N23: MCP23017.GPB6, COOL-5.anode
  N24: MCP23017.GPB7, COOL-4.anode
  N25: MCP23017.Vdd, MCP23017.RESET, EXT.pin2, 10k.Pin_1, 10k_2.Pin_1
  N26: MCP23017.Vss, 220.Pin_1, 220_2.Pin_1, 220_3.Pin_1, 220_4.Pin_1, 220_5.Pin_1, 220_6.Pin_1, 220_7.Pin_1, 220_8.Pin_1, POWER.leg1, 220_9.Pin_1, 220_10.Pin_1, 220_11.Pin_1, 220_12.Pin_0, 220_13.Pin_0, 220_14.Pin_0, 220_15.Pin_0, 220_16.Pin_1, COOLANT.EncoderPinC, EXT.pin3, 10nF.0, 10nF_2.0
  N27: MCP23017.SCL, EXT.pin4
  N28: MCP23017.SDA, EXT.pin5
  N29: POWER.wiper, EXT.pin6
  N30: POWER.leg2, EXT.pin1
  N31: COOL-0.cathode, 220_12.Pin_1
  N32: COOL-1.cathode, 220_13.Pin_1
  N33: COOL-2.cathode, 220_14.Pin_1
  N34: COOL-3.cathode, 220_15.Pin_1
  N35: COOL-4.cathode, 220_16.Pin_0
  N36: COOL-5.cathode, 220_9.Pin_0
  N37: COOL-6.cathode, 220_10.Pin_0
  N38: COOL-7.cathode, 220_11.Pin_0
  N39: COOLANT.EncoderPinA, 10k.Pin_0, 10k_3.Pin_1
  N40: COOLANT.EncoderPinB, 10k_2.Pin_0, 10k_4.Pin_1
  N41: EXT.pin7, 10nF.1, 10k_3.Pin_0
  N42: EXT.pin8, 10nF_2.1, 10k_4.Pin_0

notes:
  Coolant CW
  Coolant CCW
  SCL
  SDA
  Power POT
  GND
  5V
  zebit.fi
  Designed by Zebit
  Space Device Lab
  ADDRESS
  HIGH
  LOW
  Slider 5V

custom parts:
  MCP23017: MCP23017 16 bit port expander
