# Fritzing sketch 8-led-connection-base (saved by Fritzing 0.9.1b)
circuit board: 5.59069cm x 6.61206cm
stripboards: 1

parts:
  LED1 = LED - 5mm [color="Red (633nm)" package="5 mm [THT]"]
  LED2 = LED - 5mm [color="Red (633nm)" package="5 mm [THT]"]
  LED3 = LED - 5mm [color="Red (633nm)" package="5 mm [THT]"]
  LED5 = LED - 5mm [color="Red (633nm)" package="5 mm [THT]"]
  LED6 = LED - 5mm [color="Red (633nm)" package="5 mm [THT]"]
  LED4 = LED - 5mm [color="Red (633nm)" package="5 mm [THT]"]
  LED8 = LED - 5mm [color="Red (633nm)" package="5 mm [THT]"]
  LED7 = LED - 5mm [color="Red (633nm)" package="5 mm [THT]"]
  Heat_display = female pin header, 9 pins [form="♀ (female)"]

nets:
  N1: LED1.cathode, Heat_display.pin1
  N2: LED1.anode, LED2.anode, LED3.anode, LED5.anode, LED6.anode, LED4.anode, LED8.anode, LED7.anode, Heat_display.pin9
  N3: LED2.cathode, Heat_display.pin2
  N4: LED3.cathode, Heat_display.pin3
  N5: LED5.cathode, Heat_display.pin5
  N6: LED6.cathode, Heat_display.pin6
  N7: LED4.cathode, Heat_display.pin4
  N8: LED8.cathode, Heat_display.pin8
  N9: LED7.cathode, Heat_display.pin7

notes:
  Part number:
  TSN-ENG-101-b
