# Fritzing sketch 8-led-stripboard-prototype (saved by Fritzing 0.9.1b)
stripboards: 1

parts:
  MCP1 = MCP23017 [chip_label=MCP23017 package="DIP (Dual Inline) [THT]"]
  HEAT7 = LED - 5mm [color="Red (633nm)" package="5 mm [THT]"]
  220 = Resistor [tolerance=±5% resistance=220 package=THT]
  COOL7 = LED - 5mm [color="Red (633nm)" package="5 mm [THT]"]
  R1 = Resistor [tolerance=±5% resistance=220 package=THT]
  HEAT5 = LED - 5mm [color="Red (633nm)" package="5 mm [THT]"]
  COOL5 = LED - 5mm [color="Red (633nm)" package="5 mm [THT]"]
  R2 = Resistor [tolerance=±5% resistance=220 package=THT]
  HEAT1 = LED - 5mm [color="Red (633nm)" package="5 mm [THT]"]
  HEAT3 = LED - 5mm [color="Red (633nm)" package="5 mm [THT]"]
  220_2 = Resistor [tolerance=±5% resistance=220 package=THT]
  COOL1 = LED - 5mm [color="Red (633nm)" package="5 mm [THT]"]
  COOL3 = LED - 5mm [color="Red (633nm)" package="5 mm [THT]"]
  R3 = Resistor [tolerance=±5% resistance=220 package=THT]
  R4 = Resistor [tolerance=±5% resistance=220 package=THT]
  220_3 = Resistor [tolerance=±5% resistance=220 package=THT]
  220_4 = Resistor [tolerance=±5% resistance=220 package=THT]
  External_connections = screw terminal, 7 pins
  RE1 = Rotary Encoder [package=THT]
  R5 = Slide Potentiometer [maximum_resistance=100kΩ]

nets:
  N1: MCP1.GPB0, COOL7.anode
  N2: MCP1.GPB2, COOL5.anode
  N3: MCP1.GPB4, COOL3.anode
  N4: MCP1.GPB6, COOL1.anode
  N5: MCP1.Vdd, MCP1.RESET, External_connections.pin7, R5.leg1
  N6: MCP1.Vss, MCP1.Address_0, MCP1.Address_1, MCP1.Address_2, 220.Pin_1, R1.Pin_0, R2.Pin_0, 220_2.Pin_1, R3.Pin_0, R4.Pin_0, 220_3.Pin_1, 220_4.Pin_1, External_connections.pin6, RE1.EncoderPinC, R5.leg2
  N7: MCP1.SCL, External_connections.pin5
  N8: MCP1.SDA, External_connections.pin4
  N9: MCP1.GPA1, HEAT1.anode
  N10: MCP1.GPA3, HEAT3.anode
  N11: MCP1.GPA5, HEAT5.anode
  N12: MCP1.GPA7, HEAT7.anode
  N13: HEAT7.cathode, 220.Pin_0
  N14: COOL7.cathode, R1.Pin_1
  N15: HEAT5.cathode, 220_3.Pin_0
  N16: COOL5.cathode, R2.Pin_1
  N17: HEAT1.cathode, 220_2.Pin_0
  N18: HEAT3.cathode, 220_4.Pin_0
  N19: COOL1.cathode, R3.Pin_1
  N20: COOL3.cathode, R4.Pin_1
  N21: External_connections.pin1, RE1.EncoderPinB
  N22: External_connections.pin2, RE1.EncoderPinA
  N23: External_connections.pin3, R5.wiper

custom parts:
  MCP23017: MCP23017 16 bit port expander
