# Fritzing sketch interrupt-expander-2-encoders (saved by Fritzing 0.9.1b)
breadboards: 1

parts:
  MCP1 = MCP23017 [chip_label=MCP23017 package="DIP (Dual Inline) [THT]"]
  Part1 = Arduino Uno (Rev3)
  RE1 = Rotary Encoder [package=THT]
  R1 = Resistor [tolerance=±5% resistance=10k package=THT]
  R2 = Resistor [tolerance=±5% resistance=10k package=THT]
  RE2 = Rotary Encoder [package=THT]
  R3 = Resistor [tolerance=±5% resistance=10k package=THT]
  R4 = Resistor [tolerance=±5% resistance=10k package=THT]

nets:
  N1: MCP1.GPB0, RE2.EncoderPinB, R3.Pin_0
  N2: MCP1.GPB1, RE2.EncoderPinA, R4.Pin_0
  VDD: MCP1.Vdd, MCP1.RESET, Part1.5V, R1.Pin_1, R2.Pin_1, R3.Pin_1, R4.Pin_1
  VSS: MCP1.Vss, MCP1.Address_0, MCP1.Address_1, MCP1.Address_2, Part1.GND, RE1.EncoderPinC, RE2.EncoderPinC
  N3: MCP1.SCL, Part1.A5/SCL
  N4: MCP1.SDA, Part1.A4/SDA
  N5: MCP1.INTB, Part1.D1/TX
  N6: MCP1.INTA, Part1.D0/RX
  N7: MCP1.GPA6, RE1.EncoderPinB, R1.Pin_0
  N8: MCP1.GPA7, RE1.EncoderPinA, R2.Pin_0

custom parts:
  MCP23017: MCP23017 16 bit port expander
