# Fritzing sketch 3-led-mcp23017-testing (saved by Fritzing 0.9.1b)
breadboards: 1

parts:
  Part1 = Arduino Uno (Rev3)
  MCP1 = MCP23017 [chip_label=MCP23017 package="DIP (Dual Inline) [THT]"]  # not connected
  LED3 = LED - 5mm [color="Red (633nm)" package="5 mm [THT]"]
  R1 = Resistor [tolerance=±5% resistance=4.7k package=THT]
  R2 = Resistor [tolerance=±5% resistance=4.7k package=THT]
  LED4 = LED - 5mm [color="Red (633nm)" package="5 mm [THT]"]
  LED5 = LED - 5mm [color="Red (633nm)" package="5 mm [THT]"]
  R3 = Resistor [tolerance=±5% resistance=220 package=THT]
  R4 = Resistor [tolerance=±5% resistance=220 package=THT]
  R5 = Resistor [tolerance=±5% resistance=220 package=THT]

nets:
  N1: Part1.A4/SDA, R1.Pin_1
  N2: Part1.A5/SCL, R2.Pin_1
  N3: Part1.GND, R1.Pin_0, R2.Pin_0, R3.Pin_1, R4.Pin_1, R5.Pin_1
  N4: LED3.anode, R5.Pin_0
  N5: LED4.anode, R4.Pin_0
  N6: LED5.anode, R3.Pin_0

custom parts:
  MCP23017: MCP23017 16 bit port expander
