# Fritzing sketch usb_serial_duplex (saved by Fritzing 0.9.1b)
breadboards: 1

parts:
  Part1 = Arduino Mega ADK (Rev3)
  RE1 = Rotary Encoder [package=THT]
  R1 = Resistor [tolerance=±5% resistance=10k package=THT]
  R2 = Resistor [tolerance=±5% resistance=10k package=THT]
  R3 = Resistor [tolerance=±5% resistance=10k package=THT]
  10uF = Ceramic Capacitor [capacitance=100nF package="100 mil [THT, multilayer]"]
  10_uF = Ceramic Capacitor [capacitance=100nF package="100 mil [THT, multilayer]"]
  R4 = Resistor [tolerance=±5% resistance=10k package=THT]

nets:
  N1: Part1.A8, R2.Pin_0, 10_uF.0
  N2: Part1.A9, R3.Pin_0, 10uF.0
  N3: Part1.A10, Part1.A11, Part1.A12, Part1.A13, Part1.A14, Part1.A15, Part1.GND, Part1.D13_PWM, Part1.D12_PWM, Part1.D11_PWM, Part1.D10_PWM, Part1.D50/MISO, Part1.D51/MOSI, Part1.D52/SCK, Part1.D53/SS, RE1.EncoderPinC
  N4: Part1.5V, R1.Pin_0, 10uF.1, 10_uF.1, R4.Pin_0
  N5: RE1.EncoderPinA, R1.Pin_1, R3.Pin_1
  N6: RE1.EncoderPinB, R2.Pin_1, R4.Pin_1
